// Logisim project pipeline.circ as structural Verilog: 3 circuits, main circuit main
module main (
  output [7:0] out_1,
  output [7:0] out_2
);

  wire clock_1_out;
  wire [7:0] random_1_out, random_2_out;

  Random random_1 (.clk(clock_1_out), .out(random_1_out));  // open: next, clr
  Random random_2 (.clk(clock_1_out), .out(random_2_out));  // open: next, clr
  Clock clock_1 (.out(clock_1_out));
  // Probe on out_1
  Non_Pipelined non_pipelined_1 (.input_1(random_1_out), .input_2(random_2_out), .clock(clock_1_out), .\output (out_1));
  // Probe on out_2
  Pipelined pipelined_1 (.input_1(random_1_out), .input_2(random_2_out), .clock(clock_1_out), .\output (out_2));
endmodule

module Non_Pipelined (
  input  [7:0] input_1,
  input  [7:0] input_2,
  input  clock,
  output [7:0] \output 
);

  wire [7:0] adder_1_out, multiplier_1_out;

  Multiplier multiplier_1 (.a(input_1), .b(input_2), .out(multiplier_1_out));  // open: cin, cout
  Adder adder_1 (.a(multiplier_1_out), .b(\output ), .out(adder_1_out));  // open: cin, cout
  Register register_1 (.D(adder_1_out), .Q(\output ), .clk(clock));  // open: en, clr

  // Notes on the sheet:
  //   DO NOT MODIFY THIS CIRCUIT!
endmodule

module Pipelined (
  input  [7:0] input_1,
  input  [7:0] input_2,
  input  clock,
  output [7:0] \output 
);

  wire [7:0] adder_1_out, multiplier_1_out, register_1_q;

  Multiplier multiplier_1 (.a(input_1), .b(input_2), .out(multiplier_1_out));  // open: cin, cout
  Register register_1 (.D(multiplier_1_out), .Q(register_1_q), .clk(clock));  // open: en, clr
  Adder adder_1 (.a(register_1_q), .b(\output ), .out(adder_1_out));  // open: cin, cout
  Register register_2 (.D(adder_1_out), .Q(\output ), .clk(clock));  // open: en, clr

  // Notes on the sheet:
  //   PIPELINE THE CIRCUIT!
endmodule
