// Logisim project rotr.circ as structural Verilog: 4 circuits, main circuit main
module main (
);

  wire clock_1_out, comparator_1_eq;
  wire [3:0] random_2_out;
  wire [15:0] random_1_out, rotr_1_result, shifter_1_out;

  Clock clock_1 (.out(clock_1_out));
  Random #(.width(16)) random_1 (.clk(clock_1_out), .out(random_1_out));  // open: next, clr
  Random #(.width(4)) random_2 (.clk(clock_1_out), .out(random_2_out));  // open: next, clr
  // Probe on random_1_out
  Shifter #(.width(16), .shift("rr")) shifter_1 (.in(random_1_out), .\dist (random_2_out), .out(shifter_1_out));
  rotr rotr_1 (.data(random_1_out), .rotate_amount(random_2_out), .result(rotr_1_result));
  // Probe on random_2_out
  Comparator #(.width(16)) comparator_1 (.a(shifter_1_out), .b(rotr_1_result), .eq(comparator_1_eq));  // open: gt, lt
  // Probe on shifter_1_out
  // Probe on rotr_1_result
  LED red_if_correct (.in(comparator_1_eq));

  // Notes on the sheet:
  //   THIS TESTS YOUR "rotr" SUB-CIRCUIT BY USING RANDOM INPUTS,
  //   COMPARING YOUR SOLUTION WITH THE BUILT-IN ROTATE RIGHT
endmodule

// ROTR
module rotr (
  input  [15:0] data,
  input  [3:0] rotate_amount,
  output [15:0] result
);

  wire [15:0] A___16_b_out_3, A__B_out;

  A__B A__B (.A(data), .B(rotate_amount), .Out(A__B_out));
  A___16_B A___16_b (.A(data), .B(rotate_amount), .out_3(A___16_b_out_3));
  assign result = A__B_out | A___16_b_out_3;  // OR_Gate or_1, 16 bits wide

  // Notes on the sheet:
  //   * YOUR CIRCUIT HERE *
  //   You will DEFINITELY want to break this up into smaller sub-circuits!
endmodule

module A__B (
  input  [15:0] A,
  input  [3:0] B,
  output [15:0] Out
);

  wire [15:0] divider_1_out, divider_2_out, divider_3_out, divider_4_out, divider_5_out, divider_6_out,
       divider_7_out, divider_8_out, divider_9_out, divider_10_out, divider_11_out, divider_12_out,
       divider_13_out, divider_14_out, divider_15_out, divider_16_out;

  Divider #(.width(16)) divider_1 (.a(A), .b({16{1'b0}}), .out(divider_1_out));  // open: upper, rem
  Divider #(.width(16)) divider_2 (.a(A), .b(16'h2), .out(divider_2_out));  // open: upper, rem
  Divider #(.width(16)) divider_3 (.a(A), .b(16'h4), .out(divider_3_out));  // open: upper, rem
  Divider #(.width(16)) divider_4 (.a(A), .b(16'h8), .out(divider_4_out));  // open: upper, rem
  Divider #(.width(16)) divider_5 (.a(A), .b(16'h10), .out(divider_5_out));  // open: upper, rem
  Divider #(.width(16)) divider_6 (.a(A), .b(16'h20), .out(divider_6_out));  // open: upper, rem
  Divider #(.width(16)) divider_7 (.a(A), .b(16'h40), .out(divider_7_out));  // open: upper, rem
  Divider #(.width(16)) divider_8 (.a(A), .b(16'h80), .out(divider_8_out));  // open: upper, rem
  Divider #(.width(16)) divider_9 (.a(A), .b(16'h100), .out(divider_9_out));  // open: upper, rem
  Divider #(.width(16)) divider_10 (.a(A), .b(16'h200), .out(divider_10_out));  // open: upper, rem
  Divider #(.width(16)) divider_11 (.a(A), .b(16'h400), .out(divider_11_out));  // open: upper, rem
  Divider #(.width(16)) divider_12 (.a(A), .b(16'h800), .out(divider_12_out));  // open: upper, rem
  Divider #(.width(16)) divider_13 (.a(A), .b(16'h1000), .out(divider_13_out));  // open: upper, rem
  Divider #(.width(16)) divider_14 (.a(A), .b(16'h2000), .out(divider_14_out));  // open: upper, rem
  Divider #(.width(16)) divider_15 (.a(A), .b(16'h4000), .out(divider_15_out));  // open: upper, rem
  Divider #(.width(16)) divider_16 (.a(A), .b(16'h8000), .out(divider_16_out));  // open: upper, rem
  Multiplexer #(.select(4), .width(16)) multiplexer_1 (
    .in0(divider_1_out), .in1(divider_2_out), .in2(divider_3_out), .in3(divider_4_out), .in4(divider_5_out),
    .in5(divider_6_out), .in6(divider_7_out), .in7(divider_8_out), .in8(divider_9_out), .in9(divider_10_out),
    .in10(divider_11_out), .in11(divider_12_out), .in12(divider_13_out), .in13(divider_14_out),
    .in14(divider_15_out), .in15(divider_16_out), .out(Out), .sel(B), .en(1'b1));
endmodule

module A___16_B (
  input  [15:0] A,
  input  [3:0] B,
  output [15:0] out_3
);

  wire [3:0] adder_1_out, subtractor_1_out;
  wire [15:0] multiplier_1_out, multiplier_2_cout, multiplier_2_out, multiplier_3_out, multiplier_4_out,
       multiplier_5_out, multiplier_6_out, multiplier_7_out, multiplier_8_out, multiplier_9_out,
       multiplier_10_out, multiplier_11_out, multiplier_12_out, multiplier_13_out, multiplier_14_out,
       multiplier_15_out, multiplier_16_out;

  Subtractor #(.width(4)) subtractor_1 (.a(4'b1111), .b(B), .out(subtractor_1_out));  // open: bin, bout
  Adder #(.width(4)) adder_1 (.a(subtractor_1_out), .b(4'b0001), .out(adder_1_out));  // open: cin, cout
  Multiplier #(.width(16)) multiplier_1 (.a(A), .b({16{1'b0}}), .out(multiplier_1_out));  // open: cin, cout
  Multiplier #(.width(16)) multiplier_2 (.a(A), .out(multiplier_2_out), .cout(multiplier_2_cout));  // open: b, cin
  Multiplier #(.width(16)) multiplier_3 (.a(A), .b(16'h4), .out(multiplier_3_out));  // open: cin, cout
  Multiplier #(.width(16)) multiplier_4 (.a(A), .b(16'h8), .out(multiplier_4_out));  // open: cin, cout
  Multiplier #(.width(16)) multiplier_5 (.a(A), .b(16'h10), .out(multiplier_5_out));  // open: cin, cout
  Multiplier #(.width(16)) multiplier_6 (.a(A), .b(16'h20), .out(multiplier_6_out));  // open: cin, cout
  Multiplier #(.width(16)) multiplier_7 (.a(A), .b(16'h40), .out(multiplier_7_out));  // open: cin, cout
  Multiplier #(.width(16)) multiplier_8 (.a(A), .b(16'h80), .out(multiplier_8_out));  // open: cin, cout
  Multiplier #(.width(16)) multiplier_9 (.a(A), .b(16'h100), .out(multiplier_9_out));  // open: cin, cout
  Multiplier #(.width(16)) multiplier_10 (.a(A), .b(16'h200), .out(multiplier_10_out));  // open: cin, cout
  Multiplier #(.width(16)) multiplier_11 (.a(A), .b(16'h400), .out(multiplier_11_out));  // open: cin, cout
  Multiplier #(.width(16)) multiplier_12 (.a(A), .b(16'h800), .out(multiplier_12_out));  // open: cin, cout
  Multiplier #(.width(16)) multiplier_13 (.a(A), .b(16'h1000), .out(multiplier_13_out));  // open: cin, cout
  Multiplier #(.width(16)) multiplier_14 (.a(A), .b(16'h2000), .out(multiplier_14_out));  // open: cin, cout
  Multiplier #(.width(16)) multiplier_15 (.a(A), .b(16'h4000), .out(multiplier_15_out));  // open: cin, cout
  Multiplier #(.width(16)) multiplier_16 (.a(A), .b(16'h8000), .out(multiplier_16_out));  // open: cin, cout
  Multiplexer #(.select(4), .width(16)) multiplexer_1 (
    .in0(multiplier_1_out), .in1(multiplier_2_out), .in2(multiplier_3_out), .in3(multiplier_4_out),
    .in4(multiplier_5_out), .in5(multiplier_6_out), .in6(multiplier_7_out), .in7(multiplier_8_out),
    .in8(multiplier_9_out), .in9(multiplier_10_out), .in10(multiplier_11_out), .in11(multiplier_12_out),
    .in12(multiplier_13_out), .in13(multiplier_14_out), .in14(multiplier_15_out), .in15(multiplier_16_out),
    .out(out_3), .sel(adder_1_out), .en(1'b1));
  // also tied to GND on the sheet: {multiplier_2_cout[0], multiplier_2_cout[2], multiplier_2_cout[3], multiplier_2_cout[4], multiplier_2_cout[5], multiplier_2_cout[6], multiplier_2_cout[7], multiplier_2_cout[8], multiplier_2_cout[9], multiplier_2_cout[10], multiplier_2_cout[11], multiplier_2_cout[12], multiplier_2_cout[13], multiplier_2_cout[14], multiplier_2_cout[15]}
  // also tied to VCC on the sheet: multiplier_2_cout[1]
endmodule
