// Logisim project CMP.circ as structural Verilog: 1 circuit, main circuit main
// CMP
module main (
  input  LT,
  input  EQ,
  input  GT,
  input  [2:0] CQ_QUERY,
  input  CR_WRITE,
  input  CLOCK,
  output [2:0] CR_VAL,
  output CQ_PASSED
);

  wire s_r_ff_1_q;
  wire [2:0] and_1_out, register_1_q;

  Register #(.width(3)) register_1 (.D({LT, EQ, GT}), .en(CR_WRITE), .Q(register_1_q), .clk(CLOCK));  // open: clr
  Multiplexer #(.width(3)) multiplexer_1 (
    .in0(3'b111), .in1(register_1_q), .out(CR_VAL), .sel(s_r_ff_1_q));  // open: en
  S_R_Flip_Flop s_r_ff_1 (.S(CR_WRITE), .clk(CLOCK), .R(1'b0), .Q(s_r_ff_1_q));  // open: Qn, preset, reset, en
  // Probe on and_1_out
  assign and_1_out = CR_VAL & CQ_QUERY;  // AND_Gate and_1, 3 bits wide
  Comparator #(.width(3), .mode("unsigned")) comparator_1 (.a(and_1_out), .b(3'b000), .gt(CQ_PASSED));  // open: eq, lt

  // Other names for the same wires on the sheet: clk = CLOCK; cq[2:0] = CQ_QUERY; cr[2:0] = CR_VAL; we = CR_WRITE

  // Notes on the sheet:
  //   CR MODULE
endmodule
