// Logisim project CPU.circ as structural Verilog: 1 circuit, main circuit main
// CPU
module main (
  input  [31:0] INSTRUCTION,
  input  [23:0] CURRENT_PC,
  input  CQ_PASSED,
  input  [31:0] REG_1_VAL,
  input  [31:0] REG_2_VAL,
  input  [31:0] REG_3_VAL,
  input  [31:0] ALU_RESULT,
  input  [31:0] MEM_OUT,
  output [23:0] JUMP_ADDRESS,
  output [2:0] CQ_QUERY,
  output CR_WRITE,
  output [3:0] REG_1_READ,
  output [3:0] REG_2_READ,
  output [3:0] REG_3_WRITE,
  output [31:0] REG_WRITE_VAL,
  output REG_WRITE,
  output [31:0] ALU_SOURCE_X,
  output [31:0] ALU_SOURCE_Y,
  output [3:0] ALU_OPERATION,
  output [23:0] MEM_ADDR,
  output [31:0] MEM_IN,
  output MEM_WRITE
);

  wire and_1_out, comparator_1_eq, comparator_2_eq, comparator_3_eq, comparator_4_eq, comparator_5_eq,
       comparator_6_eq, comparator_7_gt, comparator_8_eq, comparator_9_eq, comparator_10_eq, nor_1_out;
  wire [23:0] bit_extender_1_out;
  wire [31:0] imm16, imm20, imm24, multiplexer_1_out, multiplexer_2_out, multiplexer_3_out,
       multiplexer_8_out, pc;

  Comparator #(.width(4)) comparator_1 (.a(INSTRUCTION[31:28]), .b(4'b1011), .eq(comparator_1_eq));  // open: gt, lt
  Comparator #(.width(4)) comparator_2 (.a(INSTRUCTION[31:28]), .b(4'b1101), .eq(comparator_2_eq));  // open: gt, lt
  Comparator #(.width(4)) comparator_3 (.a(INSTRUCTION[31:28]), .b(4'b1111), .eq(comparator_3_eq));  // open: gt, lt
  Comparator #(.width(4), .mode("unsigned")) comparator_4 (
    .a(INSTRUCTION[31:28]), .b(4'b1110), .eq(comparator_4_eq));  // open: gt, lt
  Comparator #(.width(4)) comparator_5 (.a(INSTRUCTION[31:28]), .b(4'b1010), .eq(comparator_5_eq));  // open: gt, lt
  // OR_Gate or_1 has open pins: in0=comparator_1_eq, in1=comparator_2_eq, in2=comparator_3_eq, out=open
  nor nor_1 (nor_1_out, comparator_1_eq, comparator_2_eq, comparator_3_eq);
  Multiplexer #(.width(32), .enable("false")) multiplexer_1 (
    .in0(REG_1_VAL), .in1(pc), .out(multiplexer_1_out), .sel(comparator_4_eq));
  Bit_Extender #(.in_width(32), .out_width(24), .\type ("sign")) bit_extender_1 (
    .in(REG_2_VAL), .out(bit_extender_1_out));
  Multiplexer #(.width(32), .enable("false")) multiplexer_2 (
    .in0(ALU_RESULT), .in1(MEM_OUT), .out(multiplexer_2_out), .sel(comparator_5_eq));
  Multiplexer #(.width(32), .enable("false")) multiplexer_3 (
    .in0(multiplexer_2_out), .in1(REG_2_VAL), .out(multiplexer_3_out), .sel(comparator_9_eq));
  Comparator #(.width(4), .mode("unsigned")) comparator_6 (
    .a(INSTRUCTION[31:28]), .b(4'b1101), .eq(comparator_6_eq));  // open: gt, lt
  Multiplexer #(.width(32), .enable("false")) multiplexer_4 (
    .in0(multiplexer_1_out), .in1(REG_3_VAL), .out(ALU_SOURCE_X), .sel(comparator_6_eq));
  Comparator #(.width(4), .mode("unsigned")) comparator_7 (
    .a(INSTRUCTION[31:28]), .b(4'b1011), .gt(comparator_7_gt));  // open: eq, lt
  Multiplexer #(.width(24), .enable("false")) multiplexer_5 (
    .in0(bit_extender_1_out), .in1(INSTRUCTION[23:0]), .out(JUMP_ADDRESS), .sel(INSTRUCTION[24]));
  Comparator #(.width(4)) comparator_8 (.a(INSTRUCTION[31:28]), .b(4'b1101), .eq(comparator_8_eq));  // open: gt, lt
  Comparator #(.width(4), .mode("unsigned")) comparator_9 (
    .a(INSTRUCTION[31:28]), .b(4'b1100), .eq(comparator_9_eq));  // open: gt, lt
  and and_1 (and_1_out, comparator_9_eq, INSTRUCTION[24]);
  Multiplexer #(.width(32), .enable("false")) multiplexer_6 (
    .in0(multiplexer_3_out), .in1(imm20), .out(REG_WRITE_VAL), .sel(and_1_out));
  Multiplexer #(.width(32), .enable("false")) multiplexer_7 (
    .in0(REG_2_VAL), .in1(multiplexer_8_out), .out(ALU_SOURCE_Y), .sel(INSTRUCTION[24]));
  Multiplexer #(.width(32), .enable("false")) multiplexer_8 (
    .in0(imm16), .in1(imm20), .out(multiplexer_8_out), .sel(comparator_7_gt));
  Bit_Extender #(.in_width(32), .out_width(24), .\type ("sign")) bit_extender_2 (.in(ALU_RESULT), .out(MEM_ADDR));
  Comparator #(.width(4)) comparator_10 (.a(INSTRUCTION[31:28]), .b(4'b1011), .eq(comparator_10_eq));  // open: gt, lt
  and and_2 (CR_WRITE, comparator_8_eq, CQ_PASSED);
  and and_3 (REG_WRITE, nor_1_out, CQ_PASSED);
  and and_4 (MEM_WRITE, comparator_10_eq, CQ_PASSED);
  assign pc = {{8{CURRENT_PC[23]}}, CURRENT_PC};  // Bit_Extender bit_extender_3
  assign imm24 = {{8{INSTRUCTION[23]}}, INSTRUCTION[23:0]};  // Bit_Extender bit_extender_4
  assign imm20 = {{12{INSTRUCTION[19]}}, INSTRUCTION[19:0]};  // Bit_Extender bit_extender_5
  assign imm16 = {{16{INSTRUCTION[15]}}, INSTRUCTION[15:0]};  // Bit_Extender bit_extender_6

  assign ALU_OPERATION = INSTRUCTION[31:28];
  assign CQ_QUERY = INSTRUCTION[27:25];
  assign MEM_IN = REG_3_VAL;
  assign REG_1_READ = INSTRUCTION[19:16];
  assign REG_2_READ = INSTRUCTION[3:0];
  assign REG_3_WRITE = INSTRUCTION[23:20];

  // Other names for the same wires on the sheet: cqp = CQ_PASSED; ja[23:0] = INSTRUCTION[23:0];
  //   ri[3:0] = INSTRUCTION[3:0]; rs[3:0] = INSTRUCTION[19:16]; rd[3:0] = INSTRUCTION[23:20]; i = INSTRUCTION[24];
  //   cq[2:0] = INSTRUCTION[27:25]; opcode[3:0] = INSTRUCTION[31:28]; reg1[31:0] = REG_1_VAL; reg2[31:0] = REG_2_VAL;
  //   reg3[31:0] = REG_3_VAL

  // Notes on the sheet:
  //   INSTRUCTION MODULE
  //   CR MODULE
  //   REGISTER FILE MODULE
  //   ALU MODULE
  //   MEMORY MODULE
endmodule
