// Logisim project NPC.circ as structural Verilog: 1 circuit, main circuit main
// NPC
module main (
  input  CQ_PASSED,
  input  [31:0] INSTRUCTION,
  input  [23:0] CURRENT_PC,
  input  [23:0] JUMP_ADDRESS,
  output [23:0] NEXT_PC
);

  wire jump;
  wire [23:0] adder_1_out, multiplexer_1_out;
  wire [31:0] and_1_out;

  Adder #(.width(24)) adder_1 (.a(CURRENT_PC), .b(24'h1), .out(adder_1_out));  // open: cin, cout
  Multiplexer #(.width(24)) multiplexer_1 (
    .in0(adder_1_out), .in1(JUMP_ADDRESS), .out(multiplexer_1_out), .sel(jump));  // open: en
  assign and_1_out = INSTRUCTION & 32'hf0000000;  // AND_Gate and_1, 32 bits wide
  Comparator #(.width(32)) comparator_1 (.a(and_1_out), .b(32'hf0000000), .eq(jump));  // open: gt, lt
  Multiplexer #(.width(24)) multiplexer_2 (
    .in0(adder_1_out), .in1(multiplexer_1_out), .out(NEXT_PC), .sel(CQ_PASSED));  // open: en

  // Other names for the same wires on the sheet: cqp = CQ_PASSED; npc[23:0] = NEXT_PC

  // Notes on the sheet:
  //   NPC MODULE
endmodule
