// Logisim project ALU.circ as structural Verilog: 1 circuit, main circuit main
// ALU
module main (
  input  [31:0] ALU_SOURCE_X,
  input  [31:0] ALU_SOURCE_Y,
  input  [3:0] ALU_OPERATION,
  output LT,
  output EQ,
  output GT,
  output [31:0] ALU_RESULT,
  output ADD_OVERFLOW,
  output SUB_OVERFLOW,
  output DIV_BY_ZERO
);

  wire and_3_out, and_4_out, and_5_out, and_6_out, not_1_out, not_2_out, not_3_out, not_4_out, not_5_out,
       not_6_out;
  wire [4:0] bit_extender_1_out, bit_extender_2_out;
  wire [31:0] add, \and , and_1_out, div, mul, multiplexer_1_out, negator_1_out, negator_2_out, \or , setUP,
       shifter_1_out, sll, srl, sub, \xor ;

  // Probe on ALU_SOURCE_X
  // Probe on ALU_SOURCE_Y
  Multiplier #(.width(32)) multiplier_1 (.a(ALU_SOURCE_X), .b(ALU_SOURCE_Y), .out(mul));  // open: cin, cout
  Multiplexer #(.width(32)) multiplexer_1 (
    .in0(ALU_SOURCE_Y), .in1(32'h1), .out(multiplexer_1_out), .sel(DIV_BY_ZERO));  // open: en
  Negator #(.width(32)) negator_1 (.in(ALU_SOURCE_X), .out(negator_1_out));
  Adder #(.width(32)) adder_1 (.a(ALU_SOURCE_X), .b(ALU_SOURCE_Y), .out(add));  // open: cin, cout
  assign and_1_out = ALU_SOURCE_X & 32'h1111;  // AND_Gate and_1, 32 bits wide
  Shifter #(.width(32)) shifter_1 (.in(ALU_SOURCE_Y), .\dist (5'b10000), .out(shifter_1_out));
  Divider #(.width(32)) divider_1 (.a(ALU_SOURCE_X), .b(multiplexer_1_out), .out(div));  // open: upper, rem
  Adder #(.width(32)) adder_2 (.a(ALU_SOURCE_Y), .b(negator_1_out), .out(sub));  // open: cin, cout
  assign setUP = and_1_out | shifter_1_out;  // OR_Gate or_1, 32 bits wide
  Multiplexer #(.select(4), .width(32)) multiplexer_2 (
    .in0(sll), .in1(srl), .in2(\and ), .in3(\or ), .in4(\xor ), .in5(setUP), .in6(mul), .in7(div), .in8(sub),
    .in9(add), .in10(add), .in11(add), .in12(add), .in13(add), .in14(add), .in15(add), .out(ALU_RESULT),
    .sel(ALU_OPERATION));  // open: en
  // Probe on ALU_RESULT
  Bit_Extender #(.in_width(32), .out_width(5)) bit_extender_1 (.in(ALU_SOURCE_Y), .out(bit_extender_1_out));
  Bit_Extender #(.in_width(32), .out_width(5)) bit_extender_2 (.in(ALU_SOURCE_Y), .out(bit_extender_2_out));
  assign \and  = ALU_SOURCE_X & ALU_SOURCE_Y;  // AND_Gate and_2, 32 bits wide
  assign \or  = ALU_SOURCE_X | ALU_SOURCE_Y;  // OR_Gate or_2, 32 bits wide
  assign \xor  = ALU_SOURCE_X ^ ALU_SOURCE_Y;  // XOR_Gate xor_1, 32 bits wide
  Shifter #(.width(32)) shifter_2 (.in(ALU_SOURCE_X), .\dist (bit_extender_1_out), .out(sll));
  Shifter #(.width(32), .shift("lr")) shifter_3 (.in(ALU_SOURCE_X), .\dist (bit_extender_2_out), .out(srl));
  Negator #(.width(32)) negator_2 (.in(ALU_SOURCE_X), .out(negator_2_out));
  not not_1 (not_1_out, ALU_SOURCE_X[31]);
  not not_2 (not_2_out, ALU_SOURCE_Y[31]);
  not not_3 (not_3_out, add[31]);
  not not_4 (not_4_out, negator_2_out[31]);
  not not_5 (not_5_out, ALU_SOURCE_Y[31]);
  not not_6 (not_6_out, sub[31]);
  Comparator #(.width(32)) comparator_1 (.a(ALU_SOURCE_X), .b(ALU_SOURCE_Y), .gt(GT), .eq(EQ), .lt(LT));
  and and_3 (and_3_out, not_1_out, not_2_out, add[31]);
  and and_4 (and_4_out, ALU_SOURCE_X[31], ALU_SOURCE_Y[31], not_3_out);
  and and_5 (and_5_out, not_4_out, not_5_out, sub[31]);
  and and_6 (and_6_out, negator_2_out[31], ALU_SOURCE_Y[31], not_6_out);
  Comparator #(.width(32)) comparator_2 (.a(ALU_SOURCE_Y), .b({32{1'b0}}), .eq(DIV_BY_ZERO));  // open: gt, lt
  // Probe on ALU_OPERATION
  or or_3 (ADD_OVERFLOW, and_3_out, and_4_out);
  or or_4 (SUB_OVERFLOW, and_5_out, and_6_out);
  // Probe on ALU_RESULT

  // Other names for the same wires on the sheet: add_over = ADD_OVERFLOW; alu_op[3:0] = ALU_OPERATION;
  //   div0 = DIV_BY_ZERO; sub_over = SUB_OVERFLOW; x[31:0] = ALU_SOURCE_X; y[31:0] = ALU_SOURCE_Y

  // Notes on the sheet:
  //   ALU MODULE
endmodule
