// Logisim project PIP.circ as structural Verilog: 1 circuit, main circuit main
// PIP
module main (
  input  CQ_PASSED,
  input  [31:0] INSTRUCTION_IN,
  input  [23:0] PC_IN,
  input  CLOCK,
  output [31:0] INSTRUCTION_OUT,
  output [23:0] PC_OUT
);

  wire comparator_1_eq, nop;
  wire [31:0] and_1_out, multiplexer_1_out;

  Multiplexer #(.width(32)) multiplexer_1 (
    .in0(INSTRUCTION_IN), .in1({32{1'b0}}), .out(multiplexer_1_out), .sel(nop));  // open: en
  Register #(.width(32)) register_1 (.D(multiplexer_1_out), .Q(INSTRUCTION_OUT), .clk(CLOCK));  // open: en, clr
  Register #(.width(24)) register_2 (.D(PC_IN), .Q(PC_OUT), .clk(CLOCK));  // open: en, clr
  assign and_1_out = INSTRUCTION_OUT & 32'hf0000000;  // AND_Gate and_1, 32 bits wide
  Comparator #(.width(32)) comparator_1 (.a(and_1_out), .b(32'hf0000000), .eq(comparator_1_eq));  // open: gt, lt
  and and_2 (nop, CQ_PASSED, comparator_1_eq);

  // Other names for the same wires on the sheet: clk = CLOCK

  // Notes on the sheet:
  //   PIPELINE MODULE
endmodule
