// Logisim project REG.circ as structural Verilog: 1 circuit, main circuit main
// REG
module main (
  input  CLOCK,
  input  [3:0] REG_1_READ,
  input  [3:0] REG_2_READ,
  input  [3:0] REG_3_WRITE,
  input  [31:0] REG_WRITE_VAL,
  input  REG_WRITE,
  output [31:0] R00,
  output [31:0] R01,
  output [31:0] R02,
  output [31:0] R03,
  output [31:0] R04,
  output [31:0] R05,
  output [31:0] R06,
  output [31:0] R07,
  output [31:0] REG_1_VAL,
  output [31:0] REG_2_VAL,
  output [31:0] REG_3_VAL,
  output [31:0] R08,
  output [31:0] R09,
  output [31:0] R10,
  output [31:0] R11,
  output [31:0] R12,
  output [31:0] R13,
  output [31:0] R14,
  output [31:0] R15
);

  wire WE00, WE01, WE02, WE03, WE04, WE05, WE06, WE07, WE08, WE09, WE10, WE11, WE12, WE13, WE14, WE15;

  // Probe on REG_1_READ
  Register #(.width(32)) register_1 (.D(REG_WRITE_VAL), .en(WE00), .Q(R00), .clk(CLOCK));  // open: clr
  Register #(.width(32)) register_2 (.D(REG_WRITE_VAL), .en(WE04), .Q(R04), .clk(CLOCK));  // open: clr
  Register #(.width(32)) register_3 (.D(REG_WRITE_VAL), .en(WE08), .Q(R08), .clk(CLOCK));  // open: clr
  Register #(.width(32)) register_4 (.D(REG_WRITE_VAL), .en(WE12), .Q(R12), .clk(CLOCK));  // open: clr
  Register #(.width(32)) register_5 (.D(REG_WRITE_VAL), .en(WE01), .Q(R01), .clk(CLOCK));  // open: clr
  Register #(.width(32)) register_6 (.D(REG_WRITE_VAL), .en(WE05), .Q(R05), .clk(CLOCK));  // open: clr
  Register #(.width(32)) register_7 (.D(REG_WRITE_VAL), .en(WE09), .Q(R09), .clk(CLOCK));  // open: clr
  Register #(.width(32)) register_8 (.D(REG_WRITE_VAL), .en(WE13), .Q(R13), .clk(CLOCK));  // open: clr
  Demultiplexer #(.select(4)) demultiplexer_1 (
    .out0(WE00), .out1(WE01), .out2(WE02), .out3(WE03), .out4(WE04), .out5(WE05), .out6(WE06), .out7(WE07),
    .out8(WE08), .out9(WE09), .out10(WE10), .out11(WE11), .out12(WE12), .out13(WE13), .out14(WE14),
    .out15(WE15), .in(REG_WRITE), .sel(REG_3_WRITE));  // open: en
  Register #(.width(32)) register_9 (.D(REG_WRITE_VAL), .en(WE02), .Q(R02), .clk(CLOCK));  // open: clr
  Register #(.width(32)) register_10 (.D(REG_WRITE_VAL), .en(WE06), .Q(R06), .clk(CLOCK));  // open: clr
  Register #(.width(32)) register_11 (.D(REG_WRITE_VAL), .en(WE10), .Q(R10), .clk(CLOCK));  // open: clr
  Register #(.width(32)) register_12 (.D(REG_WRITE_VAL), .en(WE14), .Q(R14), .clk(CLOCK));  // open: clr
  Register #(.width(32)) register_13 (.D(REG_WRITE_VAL), .en(WE03), .Q(R03), .clk(CLOCK));  // open: clr
  Register #(.width(32)) register_14 (.D(REG_WRITE_VAL), .en(WE07), .Q(R07), .clk(CLOCK));  // open: clr
  Register #(.width(32)) register_15 (.D(REG_WRITE_VAL), .en(WE11), .Q(R11), .clk(CLOCK));  // open: clr
  Register #(.width(32)) register_16 (.D(REG_WRITE_VAL), .en(WE15), .Q(R15), .clk(CLOCK));  // open: clr
  Multiplexer #(.select(4), .width(32)) multiplexer_1 (
    .in0(R00), .in1(R01), .in2(R02), .in3(R03), .in4(R04), .in5(R05), .in6(R06), .in7(R07), .in8(R08),
    .in9(R09), .in10(R10), .in11(R11), .in12(R12), .in13(R13), .in14(R14), .in15(R15), .out(REG_2_VAL),
    .sel(REG_2_READ));  // open: en
  // Probe on REG_1_VAL
  Multiplexer #(.select(4), .width(32)) multiplexer_2 (
    .in0(R00), .in1(R01), .in2(R02), .in3(R03), .in4(R04), .in5(R05), .in6(R06), .in7(R07), .in8(R08),
    .in9(R09), .in10(R10), .in11(R11), .in12(R12), .in13(R13), .in14(R14), .in15(R15), .out(REG_1_VAL),
    .sel(REG_1_READ));  // open: en
  // Probe on REG_1_READ
  Multiplexer #(.select(4), .width(32)) multiplexer_3 (
    .in0(R00), .in1(R01), .in2(R02), .in3(R03), .in4(R04), .in5(R05), .in6(R06), .in7(R07), .in8(R08),
    .in9(R09), .in10(R10), .in11(R11), .in12(R12), .in13(R13), .in14(R14), .in15(R15), .out(REG_3_VAL),
    .sel(REG_3_WRITE));  // open: en

  // Other names for the same wires on the sheet: clk = CLOCK; reg_1[3:0] = REG_1_READ; reg_2[3:0] = REG_2_READ;
  //   reg_3[3:0] = REG_3_WRITE; val2[31:0] = REG_2_VAL; val3[31:0] = REG_3_VAL; write_val[31:0] = REG_WRITE_VAL

  // Notes on the sheet:
  //   REGISTER FILE MODULE
endmodule
